# Fritzing sketch AntonelaF (saved by Fritzing 0.9.0b)
circuit board: 6.96752cm x 5.40134cm
breadboards: 1

parts:
  Parte1 = Arduino Uno (Rev3)
  LDR = Photocell (LDR) [package=THT]
  R1 = Resistor [tolerance=±5% resistance=220 package=THT]
  IC1 = IC, DIP package, 8 pins [chip_label=IC]
  C1 = Ceramic Capacitor [capacitance=100nF package="100 mil [THT, multilayer]"]
  MIC1 = Microphone
  R2 = Resistor [tolerance=±5% resistance=220 package=THT]
  R3 = Resistor [tolerance=±5% resistance=220 package=THT]
  C2 = Ceramic Capacitor [capacitance=100nF package="100 mil [THT, multilayer]"]
  R4 = Resistor [tolerance=±5% resistance=220 package=THT]
  C3 = Ceramic Capacitor [capacitance=100nF package="100 mil [THT, multilayer]"]
  R5 = Resistor [tolerance=±5% resistance=220 package=THT]
  R6 = Resistor [tolerance=±5% resistance=220 package=THT]
  R7 = Resistor [tolerance=±5% resistance=680 package=THT]

nets:
  N1: Parte1.A3, LDR.pin_1, R1.Pin_1, IC1.pin6, R6.Pin_1, R7.Pin_1
  N2: Parte1.GND, R1.Pin_0, IC1.pin4, MIC1.pin1, C2.0, R4.Pin_0, C3.0, R5.Pin_0
  N3: Parte1.5V, LDR.pin_0, IC1.pin7, R3.Pin_1, C2.1
  N4: IC1.pin2, R2.Pin_1, R6.Pin_0, R7.Pin_0
  N5: IC1.pin3, R4.Pin_1, C3.1, R5.Pin_1
  N6: C1.0, MIC1.pin2, R3.Pin_0
  N7: C1.1, R2.Pin_0
