# Fritzing sketch aseferian_tp1-corregido (saved by Fritzing 0.8.7b)
circuit board: 7.00355cm x 5.63138cm
breadboards: 1

parts:
  Parte1 = Arduino Uno (Rev3)
  LDR = Resistor [tolerance=±5% resistance=220 package=THT]
  R1 = Resistor [tolerance=±5% resistance=220 package=THT]
  R4 = Resistor [tolerance=±5% resistance=220 package=THT]
  R5 = Resistor [tolerance=±5% resistance=220 package=THT]
  LM741 = IC, DIP package, 8 pins [chip_label=IC]
  R6 = Resistor [tolerance=±5% resistance=220 package=THT]
  C2 = Ceramic Capacitor [capacitance=100nF package="100 mil [THT, multilayer]"]
  MIC = Microphone
  C1 = Ceramic Capacitor [capacitance=100nF package="100 mil [THT, multilayer]"]
  C3 = Resistor [tolerance=±5% resistance=220 package=THT]
  R3 = Resistor [tolerance=±5% resistance=220 package=THT]
  R2 = Resistor [tolerance=±5% resistance=220 package=THT]
  C4 = Ceramic Capacitor [capacitance=100nF package="100 mil [THT, multilayer]"]

nets:
  N1: Parte1.A3, LDR.Pin_1, R1.Pin_1
  N2: Parte1.A5/SCL, LM741.pin6, R6.Pin_1, C3.Pin_1
  N3: Parte1.GND, R1.Pin_0, R4.Pin_1, LM741.pin4, C2.0, MIC.pin2, C4.1
  N4: Parte1.5V, LDR.Pin_0, R5.Pin_1, LM741.pin7, R2.Pin_0, C4.0
  N5: R4.Pin_0, R5.Pin_0, LM741.pin3, C2.1
  N6: LM741.pin2, R6.Pin_0, C3.Pin_0, R3.Pin_1
  N7: MIC.pin1, C1.0, R2.Pin_1
  N8: C1.1, R3.Pin_0
