# Fritzing sketch aseferian_tp1 (saved by Fritzing 0.9.0b)
circuit board: 7.00355cm x 5.63138cm
breadboards: 1

parts:
  Parte1 = Arduino Uno (Rev3)
  LDR = Resistor [tolerance=±5% resistance=220 package=THT]
  R4 = Resistor [tolerance=±5% resistance=220 package=THT]
  Rb = Resistor [tolerance=±5% resistance=220 package=THT]
  R1 = Resistor [tolerance=±5% resistance=220 package=THT]
  IC1 = IC, DIP package, 8 pins [chip_label=IC]
  R2 = Resistor [tolerance=±5% resistance=220 package=THT]
  C1 = Ceramic Capacitor [capacitance=100nF package="100 mil [THT, multilayer]"]
  C2 = Ceramic Capacitor [capacitance=100nF package="100 mil [THT, multilayer]"]
  MIC1 = Microphone
  C3 = Ceramic Capacitor [capacitance=100nF package="100 mil [THT, multilayer]"]

nets:
  N1: Parte1.A3, LDR.Pin_1, R4.Pin_1
  N2: Parte1.A5/SCL, IC1.pin6, C2.1
  N3: Parte1.GND, R4.Pin_0, C1.0, MIC1.pin1
  N4: Parte1.5V, LDR.Pin_0, R1.Pin_1, IC1.pin2, IC1.pin3, IC1.pin4, IC1.pin7, R2.Pin_1, C1.1
  N5: Rb.Pin_0, Rb.Pin_1, R1.Pin_0, MIC1.pin2, C3.0
  N6: R2.Pin_0, C3.1
