# Fritzing sketch aller (saved by Fritzing 0.9.0b)
circuit board: 6.99842cm x 5.47926cm
breadboards: 1

parts:
  Parte1 = Arduino Uno (Rev3)
  LDR = Resistor [tolerance=±5% resistance=220 package=THT]
  R1 = Resistor [tolerance=±5% resistance=220 package=THT]
  MIC1 = Microphone
  R2 = Resistor [tolerance=±5% resistance=220 package=THT]
  C1 = Ceramic Capacitor [capacitance=100nF package="100 mil [THT, multilayer]"]
  R3 = Resistor [tolerance=±5% resistance=220 package=THT]
  R4 = Resistor [tolerance=±5% resistance=220 package=THT]
  IC1 = IC, DIP package, 8 pins [chip_label=IC]
  R5 = Resistor [tolerance=±5% resistance=220 package=THT]
  C2 = Ceramic Capacitor [capacitance=100nF package="100 mil [THT, multilayer]"]
  R6 = Resistor [tolerance=±5% resistance=220 package=THT]
  R7 = Resistor [tolerance=±5% resistance=220 package=THT]

nets:
  N1: Parte1.A3, LDR.Pin_1, R1.Pin_0
  N2: Parte1.A5/SCL, IC1.pin6, R6.Pin_1, R7.Pin_1
  N3: Parte1.GND, R1.Pin_1, MIC1.pin2, IC1.pin3, IC1.pin4, R5.Pin_0, C2.0
  N4: Parte1.5V, LDR.Pin_0, R2.Pin_0, R4.Pin_1, IC1.pin7
  N5: MIC1.pin1, R2.Pin_1, C1.0
  N6: C1.1, R3.Pin_0
  N7: R3.Pin_1, R4.Pin_0, IC1.pin2, R5.Pin_1, C2.1, R6.Pin_0, R7.Pin_0
