# Fritzing sketch Mic y LDR - Luciano Pujol - DaVinci (saved by Fritzing 0.9.0b)
circuit board: 7.00645cm x 5.48209cm
breadboards: 1

parts:
  Parte1 = Arduino Uno (Rev3)
  IC1 = IC, DIP package, 8 pins [chip_label=IC]
  R1 = Resistor [tolerance=±5% resistance=220 package=THT]
  R2 = Resistor [tolerance=±5% resistance=220 package=THT]
  R3 = Resistor [tolerance=±5% resistance=220 package=THT]
  R4 = Resistor [tolerance=±5% resistance=220 package=THT]
  R5 = Resistor [tolerance=±5% resistance=220 package=THT]
  C1 = Ceramic Capacitor [capacitance=100nF package="100 mil [THT, multilayer]"]
  C3 = Ceramic Capacitor [capacitance=100nF package="100 mil [THT, multilayer]"]
  C2 = Ceramic Capacitor [capacitance=100nF package="100 mil [THT, multilayer]"]
  C4 = Ceramic Capacitor [capacitance=100nF package="100 mil [THT, multilayer]"]
  MIC = Microphone
  Part1 = Breakout Board for Electret Microphone
  LDR = Photocell (LDR) [package=THT]
  R6 = Resistor [tolerance=±5% resistance=220 package=THT]

nets:
  N1: Parte1.A0, LDR.pin_1, R6.Pin_1
  N2: Parte1.A4/SDA, Part1.AUD
  N3: Parte1.A5/SCL, IC1.pin6, R5.Pin_1, C3.1
  GND: Parte1.GND, IC1.pin4, R3.Pin_1, C2.1, C4.1, MIC.pin1, Part1.GND, R6.Pin_0
  5V: Parte1.5V, IC1.pin7, R1.Pin_0, R2.Pin_1, C4.0, Part1.VCC, LDR.pin_0
  N4: IC1.pin2, IC1.pin3, R2.Pin_0, R3.Pin_0, R4.Pin_1, R5.Pin_0, C3.0, C2.0
  N5: R1.Pin_1, C1.0, MIC.pin2
  N6: R4.Pin_0, C1.1
