# Fritzing sketch Placa_Evaluacion_1 (saved by Fritzing 0.8.7b)
circuit board: 6.94267cm x 5.44688cm
breadboards: 1

parts:
  Parte1 = Arduino Uno (Rev3)
  LM741 = PICAXE-08 [package=THT]
  MIC = Microphone
  C1 = Ceramic Capacitor [capacitance=100nF package="100 mil [THT, multilayer]"]
  R1 = Resistor [tolerance=±5% resistance=220 package=THT]
  R2 = Resistor [tolerance=±5% resistance=220 package=THT]
  C2 = Ceramic Capacitor [capacitance=100nF package="100 mil [THT, multilayer]"]
  R3 = Resistor [tolerance=±5% resistance=220 package=THT]
  C4 = Resistor [tolerance=±5% resistance=1M package=THT]
  LDR = Photocell (LDR) [package=THT]
  R5 = Resistor [tolerance=±5% resistance=220 package=THT]
  R4 = Resistor [tolerance=±5% resistance=220 package=THT]
  R6 = Resistor [tolerance=±5% resistance=220 package=THT]
  C3 = Ceramic Capacitor [capacitance=100nF package="100 mil [THT, multilayer]"]

nets:
  N1: Parte1.A0, LM741.In/Out_1, C4.Pin_1, R4.Pin_1
  N2: Parte1.A3, LDR.pin_1, R5.Pin_1
  N3: Parte1.GND, LM741.In_3, MIC.pin1, R2.Pin_0, C2.0, R5.Pin_0, C3.1
  N4: Parte1.5V, LM741.Serial_Out_/_Out_0, R3.Pin_1, LDR.pin_0, R6.Pin_0, C3.0
  N5: LM741.Serial_In, R1.Pin_1, C4.Pin_0, R4.Pin_0
  N6: LM741.In/Out_4, R2.Pin_1, C2.1, R3.Pin_0
  N7: MIC.pin2, C1.0, R6.Pin_1
  N8: C1.1, R1.Pin_0
